# Fritzing sketch ButtonBlinkLed (saved by Fritzing 0.8.5b)
breadboards: 1

parts:
  Componente1 = Arduino Uno (Rev3)
  S1 = Pushbutton [package="[THT]"]
  R1 = Resistor [tolerance=±5% resistance=10k package=THT]
  LED1 = LED - 5mm [color="Red (633nm)" package="5 mm [THT]"]
  R2 = Resistor [tolerance=±5% resistance=470 package=THT]

nets:
  N1: Componente1.D8, LED1.cathode
  N2: Componente1.D2, S1.Pin_1, S1.Pin_2, R1.Pin_0
  N3: Componente1.5V, S1.Pin_3, S1.Pin_4
  N4: Componente1.GND, R1.Pin_1, R2.Pin_1
  N5: LED1.anode, R2.Pin_0
